# Fritzing sketch PRG32-PCB-0-1 (saved by Fritzing 1.0.8)
circuit board: 21cm x 7.5cm
breadboards: 1

parts:
  ESP32-C6 = ESP32-C6-DevKitC-1
  MAX98357A_left = Adafruit MAX98357A I2S 3W Class D Amplifier [part_number="Adafruit #3006"]
  Left_speaker = SPEAKER [package=pcb_mount_speaker]
  Right_speaker = SPEAKER [package=pcb_mount_speaker]
  ILI9341_TFT = 2.8" SPI TFT Module [part_number=MSP2807]
  Joystick = JOYSTICK_MINI [package=joystick_mini]
  MAX98357A_right = Adafruit MAX98357A I2S 3W Class D Amplifier [part_number="Adafruit #3006"]
  A = SWITCH-MOMENTARY-2 [package=tactile_switch_smd-2]
  B = SWITCH-MOMENTARY-2 [package=tactile_switch_smd-2]
  Right_channel_mode = Resistor [tolerance=±5% resistance=390k package="1206 [SMD]"]

nets:
  N1: ESP32-C6.Pin_1, ILI9341_TFT.pin1
  N2: ESP32-C6.Pin_3, MAX98357A_left.BCLK, MAX98357A_right.BCLK
  N3: ESP32-C6.Pin_4, ILI9341_TFT.pin8
  N4: ESP32-C6.Pin_5, ILI9341_TFT.pin7
  N5: ESP32-C6.Pin_6, ILI9341_TFT.pin6
  N6: ESP32-C6.Pin_7, ILI9341_TFT.pin4
  N7: ESP32-C6.Pin_8, ILI9341_TFT.pin5
  N8: ESP32-C6.Pin_10, ILI9341_TFT.pin3
  N9: ESP32-C6.Pin_11, MAX98357A_left.LRCLK, MAX98357A_right.LRCLK
  N10: ESP32-C6.Pin_12, ILI9341_TFT.pin9
  N11: ESP32-C6.Pin_13, Joystick.UP
  VIN: ESP32-C6.Pin_14, MAX98357A_left.VIN, MAX98357A_left.SD_MODE, MAX98357A_right.VIN, Right_channel_mode.Pin_0
  GND: ESP32-C6.Pin_15, ESP32-C6.Pin_18, ESP32-C6.Pin_32, MAX98357A_left.GND, ILI9341_TFT.pin2, Joystick.GND, MAX98357A_right.GND, A.2, B.2
  N12: ESP32-C6.Pin_20, Joystick.DOWN
  N13: ESP32-C6.Pin_23, Joystick.LEFT
  N14: ESP32-C6.Pin_24, Joystick.RIGHT
  N15: ESP32-C6.Pin_25, Joystick.CENT
  N16: ESP32-C6.Pin_26, A.1
  N17: ESP32-C6.Pin_27, B.1
  N18: ESP32-C6.Pin_28, MAX98357A_left.DIN, MAX98357A_right.DIN
  N19: MAX98357A_left.VO-, Left_speaker.-
  N20: MAX98357A_left.VO+, Left_speaker.+
  N21: Right_speaker.+, MAX98357A_right.VO+
  N22: Right_speaker.-, MAX98357A_right.VO-
  N23: MAX98357A_right.SD_MODE, Right_channel_mode.Pin_1

custom parts:
  ESP32-C6-DevKitC-1: ESP32-C6-DevKitC-1 is an entry-level development board based on ESP32-C6-WROOM-1(U), a general-purpose module with a 8 MB SPI flash. This board integrates complete Wi-Fi, Bluetooth LE, Zigbee, and Thread functions.
  Adafruit MAX98357A I2S 3W Class D Amplifier: Listen to this good news - we now have an all in one digital audio amp breakout board that works incredibly well with the Raspberry Pi! If you're looking for an easy and low cost way to get you digital sound files bumpin' then the MAX08357 I2S Amp Breakout is for you. It takes standard I2S digital audio input and, not only decodes it into analog, but also amplifies it directly into a speaker.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
  2.8" SPI TFT Module: A generic 2.8 inch LCD TFT 320x240 display with touchscreen and SD card slot. Uses the ILI9341 controller, like the Adafruit displays of this size uses.
