# Fritzing sketch PRG32-PCB-0-1 (saved by Fritzing 1.0.8)
breadboards: 1

parts:
  A1 = ESP32-C6-DevKitC-1
  Part1 = Adafruit MAX98357A I2S 3W Class D Amplifier [part_number="Adafruit #3006"]
  SP1 = SPEAKER [package=pcb_mount_speaker]
  SP2 = SPEAKER [package=pcb_mount_speaker]
  LCD1 = 2.8" SPI TFT Module [part_number=MSP2807]
  S1 = JOYSTICK_MINI [package=joystick_mini]
  Part2 = Adafruit MAX98357A I2S 3W Class D Amplifier [part_number="Adafruit #3006"]
  S2 = SWITCH-MOMENTARY-2 [package=tactile_switch_smd-2]
  S3 = SWITCH-MOMENTARY-2 [package=tactile_switch_smd-2]
  S4 = SWITCH-MOMENTARY-2 [package=tactile_switch_smd-2]
  R1 = Resistor [tolerance=±5% resistance=47k package="1206 [SMD]"]

nets:
  N1: A1.Pin_1, LCD1.pin1
  N2: A1.Pin_3, Part1.BCLK, Part2.BCLK
  N3: A1.Pin_4, LCD1.pin8
  N4: A1.Pin_5, LCD1.pin7
  N5: A1.Pin_6, LCD1.pin6
  N6: A1.Pin_9, LCD1.pin5
  N7: A1.Pin_10, LCD1.pin3
  N8: A1.Pin_11, Part1.LRCLK, Part2.LRCLK
  N9: A1.Pin_12, LCD1.pin9
  N10: A1.Pin_13, S1.UP
  VIN: A1.Pin_14, Part1.VIN, Part1.SD_MODE, Part2.VIN, R1.Pin_0
  GND: A1.Pin_15, A1.Pin_18, A1.Pin_32, Part1.GND, LCD1.pin2, S1.GND, Part2.GND, S2.2, S3.2, S4.2
  N11: A1.Pin_20, S1.DOWN
  N12: A1.Pin_22, LCD1.pin4, Part2.DIN
  N13: A1.Pin_23, S1.LEFT
  N14: A1.Pin_24, S1.RIGHT
  N15: A1.Pin_25, S1.CENT
  N16: A1.Pin_26, S2.1
  N17: A1.Pin_27, S3.1
  N18: A1.Pin_28, Part1.DIN
  N19: A1.Pin_29, S4.1
  N20: Part1.VO-, SP1.-
  N21: Part1.VO+, SP1.+
  N22: SP2.+, Part2.VO+
  N23: SP2.-, Part2.VO-
  N24: Part2.SD_MODE, R1.Pin_1

custom parts:
  ESP32-C6-DevKitC-1: ESP32-C6-DevKitC-1 is an entry-level development board based on ESP32-C6-WROOM-1(U), a general-purpose module with a 8 MB SPI flash. This board integrates complete Wi-Fi, Bluetooth LE, Zigbee, and Thread functions.
  Adafruit MAX98357A I2S 3W Class D Amplifier: Listen to this good news - we now have an all in one digital audio amp breakout board that works incredibly well with the Raspberry Pi! If you're looking for an easy and low cost way to get you digital sound files bumpin' then the MAX08357 I2S Amp Breakout is for you. It takes standard I2S digital audio input and, not only decodes it into analog, but also amplifies it directly into a speaker.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
  2.8" SPI TFT Module: A generic 2.8 inch LCD TFT 320x240 display with touchscreen and SD card slot. Uses the ILI9341 controller, like the Adafruit displays of this size uses.
